# Fritzing sketch APRS-Tracker (saved by Fritzing 0.9.2b)
circuit board: 6.67456cm x 5.58094cm
breadboards: 1

parts:
  Part1 = Arduino Nano (Rev3.0)
  Q1 = MOSFET-NCHANNEL [package=to220v]
  R1 = Resistor [tolerance=±5% resistance=10k package=THT]
  JP1 = Header 2 [part_number="Pin1= PTT V+,  Pin2= Gnd." package=jst-2-pth]
  R2 = Resistor [tolerance=±5% resistance=100k package=THT]
  R3 = Resistor [tolerance=±5% resistance=100k package=THT]
  C1 = Ceramic Capacitor [capacitance=1µF package="100 mil [THT, multilayer]"]
  JP2 = Header 2 [part_number="pin 1 = Line In,   Pin 2 = Gnd" package=jst-2-pth-kit]
  R4 = Resistor [tolerance=±5% resistance=8.8k package=THT]
  R5 = Resistor [tolerance=±5% resistance=3.9k package=THT]
  R6 = Resistor [tolerance=±5% resistance=2.2k package=THT]
  R7 = Resistor [tolerance=±5% resistance=1k package=THT]
  R8 = Resistor [tolerance=±5% resistance=270 package=THT]
  C2 = Ceramic Capacitor [capacitance="100 nF" package="1206 [SMD, multilayer]"]
  C3 = Ceramic Capacitor [capacitance=4.7µF package="1206 [SMD, multilayer]"]
  R9 = Resistor [tolerance=±5% resistance=1k package=THT]
  R10 = Trimmer Potentiometer [maximum_resistance=100k package=THT]
  JP3 = Header 2 [part_number="Pin1 = Line Out, Pin2 = Mic Out (use this)" package=jst-2-pth]
  U1 = EM408_CON [part_number="Commodity GPS module.  hook up VCC/Gnd where you can." package=em408_con]
  Grove1 = Grove OLED 128x96 [part_number="I use an OLED display from JFF.  SCL=A5, SDA=A4"]
  LED1 = smd LED [color="Red (633nm)" package="1206 [SMD]"]
  R11 = Resistor [tolerance=±5% resistance=220 package=THT]
  S1 = SWITCH-MOMENTARY-2 [package=tactile_switch_smd-2]

nets:
  GND: Part1.GND, Q1.S, R1.Pin_1, JP1.2, R3.Pin_1, JP2.2, R8.Pin_1, C2.0, R9.Pin_1, U1.GND, Grove1.GND, R11.Pin_1
  N1: Part1.D2, LED1.anode
  N2: Part1.D3, Q1.G, R1.Pin_0
  N3: Part1.D4, R4.Pin_0
  N4: Part1.D5, R5.Pin_0
  N5: Part1.D6, R6.Pin_0
  N6: Part1.D7, R7.Pin_0
  N7: Part1.D8, S1.1
  N8: Part1.D11/MOSI, U1.TX
  N9: Part1.D12/MISO, U1.RX
  5V: Part1.VIN, R2.Pin_0, U1.VCC, Grove1.VCC, S1.2
  N10: Part1.A5, Grove1.SCL
  N11: Part1.A4, Grove1.SDA
  N12: Part1.A0, R2.Pin_1, R3.Pin_0, C1.0
  N13: Q1.D, JP1.1
  N14: C1.1, JP2.1
  N15: R4.Pin_1, R5.Pin_1, R6.Pin_1, R7.Pin_1, R8.Pin_0, C2.1, C3.0
  N16: C3.1, R10.wiper, JP3.1
  N17: R9.Pin_0, R10.leg2, JP3.2
  N18: LED1.cathode, R11.Pin_0

notes:
  Build a 5v Buss and a Gnd Buss and hook up how you will.
